# Fritzing sketch wiring (saved by Fritzing 0.9.3b)

parts:
  Bauteil3 = Arduino Pro Mini (5V)
  R1 = Resistor [tolerance=±5% resistance=330 package="2010 [SMD]"]
  LED2 = LED - 3mm [color="Red (633nm)" package="3 mm [THT]"]
  S3 = Momentary Switch [package=ksa_sealed_tac_switch]
  VCC1 = Battery
  U1 = CC1101 [part_number=CC1101]
  U2 = MLX90614 [package=to-39]

nets:
  N1: Bauteil3.A4, U2.PWM_SDA
  N2: Bauteil3.A5, U2.SCL_VZ
  GND: Bauteil3.GND, LED2.cathode, S3.3, VCC1.-, U1.2, U2.VSS
  N3: Bauteil3.VCC, VCC1.+, U1.1
  N4: Bauteil3.SCK, U1.4
  N5: Bauteil3.MISO, U1.5
  N6: Bauteil3.MOSI, U1.3
  N7: Bauteil3.D10, U1.8
  N8: Bauteil3.D8, S3.1
  N9: Bauteil3.D6, U2.VDD
  N10: Bauteil3.D4, R1.Pin_1
  N11: Bauteil3.D2, U1.7
  N12: R1.Pin_0, LED2.anode
